# Fritzing sketch Temperatura (saved by Fritzing 0.9.3b)

parts:
  DHT1 = DHT11 Humitidy and Temperature Sensor
  part = Resistor [tolerance=±5% resistance=220 package=THT]  # not connected
  Part1 = Arduino Uno (Rev3)

nets:
  VDD: DHT1.VDD, Part1.5V
  N1: DHT1.DATA, Part1.A0
  GND: DHT1.GND, Part1.GND

custom parts:
  DHT11 Humitidy and Temperature Sensor: DHT11 Humidity and Temperature Sensor
