# Fritzing sketch Comunicacion_Wire (saved by Fritzing 0.9.3b)

parts:
  DHT1 = DHT11 Humitidy and Temperature Sensor
  Part1 = Arduino Uno (Rev3)
  Raspberry_Pi1 = Raspberry Pi 2

nets:
  VDD: DHT1.VDD, Part1.5V
  N1: DHT1.DATA, Part1.A0
  GND: DHT1.GND, Part1.GND, Raspberry_Pi1.GND
  N2: Part1.A4/SDA, Raspberry_Pi1.GPIO2
  N3: Part1.A5/SCL, Raspberry_Pi1.GPIO3

custom parts:
  DHT11 Humitidy and Temperature Sensor: DHT11 Humidity and Temperature Sensor
